// Logisim project DSD_CS23B1038.circ as structural Verilog: 1 circuit, main circuit main
module main (
  input  C0,
  input  [3:0] A,
  input  [3:0] B,
  output out_4,
  output [3:0] out_5
);

  wire and_1_out, and_2_out, and_3_out, and_4_out, and_5_out, and_6_out, and_7_out, and_8_out, and_9_out,
       and_10_out, C1_out, C2_out, C3_out, G0_out, G1_out, G2_out, G3_out, P0_out, P1_out, P2_out, P3_out;

  xor P3 (P3_out, A[3], B[3]);
  xor P0 (P0_out, A[0], B[0]);
  and G0 (G0_out, B[0], A[0]);
  xor P1 (P1_out, A[1], B[1]);
  and G1 (G1_out, A[1], B[1]);
  and G2 (G2_out, A[2], B[2]);
  xor P2 (P2_out, B[2], A[2]);
  and G3 (G3_out, A[3], B[3]);
  and and_1 (and_1_out, C0, P0_out);
  and and_2 (and_2_out, G0_out, P1_out);
  and and_3 (and_3_out, C0, P1_out, P0_out);
  and and_4 (and_4_out, P2_out, G1_out);
  and and_5 (and_5_out, P2_out, P1_out, G0_out);
  and and_6 (and_6_out, P2_out, P1_out, P0_out, C0);
  or C2 (C2_out, and_2_out, and_3_out, G1_out);
  and and_7 (and_7_out, G2_out, P3_out);
  and and_8 (and_8_out, G1_out, P2_out, P3_out);
  and and_9 (and_9_out, P3_out, P2_out, P1_out, G0_out);
  and and_10 (and_10_out, P3_out, P2_out, P1_out, P0_out, C0);
  or C1 (C1_out, and_1_out, G0_out);
  or C3 (C3_out, G2_out, and_4_out, and_5_out, and_6_out);
  xor xor_1 (out_5[0], C0, P0_out);
  xor xor_2 (out_5[1], C1_out, P1_out);
  xor xor_3 (out_5[2], C2_out, P2_out);
  or C4 (out_4, G3_out, and_7_out, and_8_out, and_9_out, and_10_out);
  xor xor_4 (out_5[3], C3_out, P3_out);
endmodule
